# Fritzing sketch esp32_garage (saved by Fritzing 0.9.3b)

parts:
  M1 = DOIT Esp32 DevKit v1 (30 pins long, 11 pins width) [part_number=ESP32S-PIN30]
  Relay = KY-019 5V Relay Module [package="Breakout board"]
  Magnetic_reed_switch_for_door_sensor = Reed switch [package=THT]
  Garage_door_opener_contacts = female pin header, 2 pins [form="♀ (female)"]
  leak_sensor_probe_(<_1m_cable) = female pin header, 2 pins [form="♀ (female)"]
  Piezo_buzzer = Piezo Speaker
  AHT-10 = Adafruit BME280
  SSD1307 = OLED 128x64 I2C Monochrome Display

nets:
  3V3: M1.3V3, AHT-10.3.3V, SSD1307.VDD
  GND: M1.GND, Relay.-, Magnetic_reed_switch_for_door_sensor.pin_1, leak_sensor_probe_(<_1m_cable).pin2, Piezo_buzzer.pin1, AHT-10.GND, SSD1307.GND
  N1: M1.D15, leak_sensor_probe_(<_1m_cable).pin1
  N2: M1.D4, Magnetic_reed_switch_for_door_sensor.pin_2
  N3: M1.D21, AHT-10.SDI/SDA, SSD1307.SDA
  N4: M1.D22, AHT-10.SCK/SCL, SSD1307.SCK
  N5: M1.D32, Piezo_buzzer.pin2
  N6: M1.D13, Relay.S
  N7: M1.VIN, Relay.+
  N8: Relay.Common, Garage_door_opener_contacts.pin2
  N9: Relay.NO, Garage_door_opener_contacts.pin1

custom parts:
  DOIT Esp32 DevKit v1 (30 pins long, 11 pins width): The DOIT Esp32 DevKit v1 is one of the development board created by DOIT to evaluate the ESP-WROOM-32 module. It is based on the ESP32 microcontroller that boasts Wifi, Bluetooth, Ethernet and Low Power support all in a single chip. (vanepp) made breadboard work, adjusted pin numbering and labels and reduced size of schematic and cleaned up pcb. This chip is 30pins long (2 x15) and 11 pins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
  KY-019 5V Relay Module: KY-019 5V Relay module, used to control AC circuits. (Special thanks to vanepp for fixing the PCB holes and other errors)
  Adafruit BME280: Bosch has stepped up their game with their new BME280 sensor, an environmental sensor with temperature, barometric pressure and humidity! This sensor is great for all sorts of weather/environmental sensing and can even be used in both I2C and SPI! This precision sensor from Bosch is the best low-cost sensing solution for measuring humidity with ±3% accuracy, barometric pressure with ±1 hPa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
